# Fritzing sketch chambre (saved by Fritzing 0.9.3b)
breadboards: 1

parts:
  U1 = ESP32S-HiLetgo [part_number=ESP32S-HiLetgo]
  7_Segment_4_Digit_Display1 = 7-SEGMENT-4DIGIT common anode [part_number="5461BS - 5462BS" package=7-segment-4digit-anode]
  Composant2 = Adafruit DS1307 RTC Breakout [part_number="Adafruit #264"]
  R1 = Resistor [tolerance=±5% resistance=220 package=THT]
  R2 = Resistor [tolerance=±5% resistance=220 package=THT]
  R3 = Resistor [tolerance=±5% resistance=220 package=THT]
  R4 = Resistor [tolerance=±5% resistance=220 package=THT]
  DHT1 = DHT11 Humitidy and Temperature Sensor

nets:
  N1: U1.GPIO35, DHT1.DATA
  N2: U1.GPIO32, 7_Segment_4_Digit_Display1.pin_10
  N3: U1.GPIO33, 7_Segment_4_Digit_Display1.pin_9
  N4: U1.GPIO25, 7_Segment_4_Digit_Display1.pin_8
  N5: U1.GPIO26, 7_Segment_4_Digit_Display1.pin_6
  N6: U1.GPIO27, 7_Segment_4_Digit_Display1.pin_2
  N7: U1.GPIO14, 7_Segment_4_Digit_Display1.pin_3
  GND: U1.GND, Composant2.GND
  N8: U1.GPIO13, R1.Pin_1
  VIN: U1.VIN, DHT1.VDD
  N9: U1.GPIO4, R3.Pin_0
  N10: U1.GPIO16, 7_Segment_4_Digit_Display1.pin_11
  N11: U1.GPIO17, 7_Segment_4_Digit_Display1.pin_12
  N12: U1.GPIO18, R2.Pin_0
  N13: U1.GPIO19, R4.Pin_0
  N14: U1.GPIO21, Composant2.SDA
  N15: U1.GPIO22, Composant2.SCL
  N16: 7_Segment_4_Digit_Display1.pin_1, R4.Pin_1
  N17: 7_Segment_4_Digit_Display1.pin_4, R2.Pin_1
  N18: 7_Segment_4_Digit_Display1.pin_5, R1.Pin_0
  N19: 7_Segment_4_Digit_Display1.pin_7, R3.Pin_1

custom parts:
  ESP32S-HiLetgo: HiLetgo ESP-WROOM-32 ESP32 ESP-32S Development Board 2.4GHz Dual-Mode WiFi + Bluetooth Dual Cores Microcontroller The ESP32 integrated with Antenna switches, RF Balun, power amplifiers, low-noise amplifiers, filters, and management modules, and the entire solution occupies the least area of PCB. 2.4 GHz Wi-Fi plus Bluetooth dual-mode chip, with TSMC Ultra-low power consumption 40nm technology,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
  7-SEGMENT-4DIGIT common anode: A 7 Segment 4 Digit common anode display, with decimal points
  Adafruit DS1307 RTC Breakout: This is a great battery-backed real time clock (RTC) that allows your microcontroller project to keep track of time even if it is reprogrammed, or if the power is lost. Perfect for datalogging, clock-building, time stamping, timers and alarms, etc. The DS1307 is the most popular RTC - but it requires 5V power to work (although we've used it with 5V power and 3.3V logic successfully) PCB &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
  DHT11 Humitidy and Temperature Sensor: DHT11 Humidity and Temperature Sensor
