# Fritzing sketch cuisine (saved by Fritzing 0.9.3b)
breadboards: 1

parts:
  DHT1 = DHT22 Humidity and Temperature Sensor
  J1 = Basic Servo
  LED1 = LED - 5mm [color="Yellow (585nm)" package="5 mm [THT]"]
  LED3 = LED - 5mm [color="Yellow (592nm)" package="5 mm [THT]"]
  LED4 = LED - 5mm [color="Yellow (595nm)" package="5 mm [THT]"]
  U1 = ESP32S-HiLetgo [part_number=ESP32S-HiLetgo]
  Keyes1 = Keyes IR Infrared Sensor Switch Module
  Keyes2 = Keyes IR Infrared Sensor Switch Module
  R1 = Resistor [tolerance=±5% resistance=220 package=THT]

nets:
  VCC: DHT1.VDD, J1.vcc, LED1.cathode, LED3.cathode, LED4.cathode, U1.VIN, Keyes1.VCC, Keyes2.VCC
  N1: DHT1.DATA, U1.GPIO27
  GND: DHT1.GND, J1.gnd, U1.GND, Keyes1.GND, Keyes2.GND
  N2: J1.pulse, U1.GPIO13
  N3: LED1.anode, LED4.anode, R1.Pin_0
  N4: U1.GPIO25, R1.Pin_1
  N5: U1.GPIO16, Keyes2.out
  N6: U1.GPIO21, Keyes1.out

custom parts:
  ESP32S-HiLetgo: HiLetgo ESP-WROOM-32 ESP32 ESP-32S Development Board 2.4GHz Dual-Mode WiFi + Bluetooth Dual Cores Microcontroller The ESP32 integrated with Antenna switches, RF Balun, power amplifiers, low-noise amplifiers, filters, and management modules, and the entire solution occupies the least area of PCB. 2.4 GHz Wi-Fi plus Bluetooth dual-mode chip, with TSMC Ultra-low power consumption 40nm technology,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
  Keyes IR Infrared Sensor Switch Module: An infrared obstacle detector
